# Fritzing sketch circuit (saved by Fritzing 0.9.5d)
breadboards: 1

parts:
  Part1 = Arduino Nano (Rev3.0)
  DRV_1 = DRV 8825 Stepper Motor Carrier, High Current [part_number="DRV 8825"]  # not connected
  M1 = RioRand LM2596
  M2 = Stepper Motor - Unipolar  # not connected
  S1 = Pushbutton [package=THT]
  R1 = Resistor [tolerance=±5% resistance=10k package="0805 [SMD]"]
  HC-SR04_Sensor_1 = HC-SR04 Ultrasonic Distance Sensor
  U1 = RELAY [package=relay-g5q]
  J2 = Power Jack [package=power_jack_smd]

nets:
  GND: Part1.GND, M1.Pin_4, R1.Pin_0, HC-SR04_Sensor_1.GND, U1.COIL1
  N1: Part1.D6, HC-SR04_Sensor_1.ECHO
  N2: Part1.D7, HC-SR04_Sensor_1.TRIG
  N3: Part1.D8, S1.leg0, R1.Pin_1
  VIN: Part1.VIN, M1.Pin_3, S1.leg1, HC-SR04_Sensor_1.VCC
  N4: M1.Pin_1, J2.GNDBREAK
  N5: M1.Pin_2, J2.GND

notes:
  24v Input
  5v output
  IoT Relay
  Limit Switch
